# Fritzing sketch TerraceLightsBoardsIntegrator (saved by Fritzing 0.9.2b)
circuit board: 3.49867cm x 4.04309cm

parts:
  ESP8266-01 = double row female pin header, 8 pins [form="♀ (female)"]
  GND_VCC_JD-VCC = female pin header, 3 pins [form="♀ (female)"]
  VCC_IN2_IN1_GND = female pin header, 4 pins [form="♀ (female)"]
  JD-VCC_VCC_GND = male pin header, 3 pins [form="♂ (male)"]
  GND_IN1_IN2_VCC = male pin header, 4 pins [form="♂ (male)"]
  C2-100uF = Capacitor [part_number=10uf package=0402-cap]
  C1-10uF = Capacitor [part_number=100uF package=0402-cap]
  LD1117_3_3v = Voltage Regulator AMS1117 [package=sot223]
  R2 = Resistor [tolerance=±5% resistance=3.3k package="0402 [SMD]"]
  R1 = Resistor [tolerance=±5% resistance=3.3k package="0402 [SMD]"]
  R3 = Resistor [tolerance=±5% resistance=3.3k package="0402 [SMD]"]
  R4 = Resistor [tolerance=±5% resistance=3.3k package="0402 [SMD]"]
  HLK-PM1 = HLK-PM01
  220v = Screw terminal - 2 pins [package=THT]

nets (from the schematic view):
  N1: ESP8266-01.pin2, R3.Pin_0
  N2: ESP8266-01.pin3, R4.Pin_0
  N3: ESP8266-01.pin4, C2-100uF.1, LD1117_3_3v.OUT, R2.Pin_0, R1.Pin_0, R3.Pin_1, R4.Pin_1
  N4: ESP8266-01.pin6, VCC_IN2_IN1_GND.pin2, GND_IN1_IN2_VCC.pin2, R2.Pin_1
  N5: ESP8266-01.pin7, VCC_IN2_IN1_GND.pin3, GND_IN1_IN2_VCC.pin3, R1.Pin_1
  N6: ESP8266-01.pin8, GND_VCC_JD-VCC.pin3, VCC_IN2_IN1_GND.pin1, JD-VCC_VCC_GND.pin3, GND_IN1_IN2_VCC.pin1, C2-100uF.2, C1-10uF.2, LD1117_3_3v.GND, HLK-PM1.-Vo
  N7: GND_VCC_JD-VCC.pin1, JD-VCC_VCC_GND.pin1
  N8: GND_VCC_JD-VCC.pin2, VCC_IN2_IN1_GND.pin4, JD-VCC_VCC_GND.pin2, GND_IN1_IN2_VCC.pin4, C1-10uF.1, LD1117_3_3v.IN, HLK-PM1.+Vo
  N9: HLK-PM1.AC#0, 220v.pin2
  N10: HLK-PM1.AC#1, 220v.pin1

notes:
  TX | GND
  CH_PD | GPIO2
  RST | GPIO0
  VCC | RX
  2 Relay Module Interface
  !!! 220v !!!
  !!! DANGER !!!
  2 Relay Module
  'ESP8266-01'
  Integrator v1.0

custom parts:
  HLK-PM01: AC-DC 220V to 5V Step-Down Power Supply Module
